# Fritzing sketch Hello_Led Fritzing (saved by Fritzing 0.9.3b)
breadboards: 1

parts:
  Parça1 = Arduino Uno (Rev3)
  LED1 = LED - 5mm [color="Red (633nm)" package="5 mm [THT]"]
  R1 = Resistor [tolerance=±5% resistance=220 package=THT]

nets:
  N1: Parça1.D4, LED1.anode
  N2: Parça1.GND, R1.Pin_1
  N3: LED1.cathode, R1.Pin_0
